// Logisim project AULA LAB1.circ as structural Verilog: 3 circuits, main circuit main
module main (
  input  [3:0] A,
  input  [3:0] OVERFLOW,
  input  OVERFLOW_2,
  input  A_2,
  input  A_3,
  input  VEM,
  output out_7,
  output out_8,
  output out_9,
  output Soma,
  output out_11,
  output out_12
);

  wire add_1_2_s, add_1_3_s, add_1_4_s;

  ADD_1 add_1_1 (.A(A[3]), .B(OVERFLOW[2]), .VEM_1(add_1_2_s), .S(OVERFLOW_2), .VAI_1(out_7));
  ADD_1 add_1_2 (.A(A[2]), .B(OVERFLOW[0]), .VEM_1(add_1_3_s), .S(add_1_2_s), .VAI_1(out_8));
  ADD_1 add_1_3 (.A(A[1]), .B(OVERFLOW[1]), .VEM_1(add_1_4_s), .S(add_1_3_s), .VAI_1(out_9));
  ADD_1 add_1_4 (.A(A[0]), .B(OVERFLOW[3]), .VEM_1(1'b0), .S(add_1_4_s), .VAI_1(Soma));
  ADD_1 add_1_5 (.A(A_2), .B(A_3), .VEM_1(VEM), .S(out_11), .VAI_1(out_12));
endmodule

module ADD_1 (
  input  A,
  input  B,
  input  VEM_1,
  output S,
  output VAI_1
);

  wire and_1_out, and_2_out, and_3_out, and_4_out, and_5_out, and_6_out, and_7_out, not_1_out, not_2_out,
       not_3_out, not_4_out, not_5_out, not_6_out;

  not not_1 (not_1_out, A);
  not not_2 (not_2_out, B);
  not not_3 (not_3_out, A);
  not not_4 (not_4_out, VEM_1);
  not not_5 (not_5_out, B);
  not not_6 (not_6_out, VEM_1);
  and and_1 (and_1_out, B, VEM_1);
  and and_2 (and_2_out, A, VEM_1);
  and and_3 (and_3_out, A, B);
  and and_4 (and_4_out, not_1_out, not_2_out, VEM_1);
  and and_5 (and_5_out, not_3_out, B, not_4_out);
  and and_6 (and_6_out, A, not_5_out, not_6_out);
  and and_7 (and_7_out, A, B, VEM_1);
  or or_1 (VAI_1, and_1_out, and_2_out, and_3_out);
  or or_2 (S, and_4_out, and_5_out, and_6_out, and_7_out);
endmodule

module ADD_2 (
  input  in_1
);
endmodule
