// Logisim project AULA LAB2V2.circ as structural Verilog: 4 circuits, main circuit main
// Add-1
module ADD_1 (
  input  A,
  input  B,
  input  VEM_1,
  output S,
  output VAI_1
);

  wire and_1_out, and_2_out, and_3_out, and_4_out, and_5_out, and_6_out, and_7_out, not_1_out, not_2_out,
       not_3_out, not_4_out, not_5_out, not_6_out;

  not not_1 (not_1_out, A);
  not not_2 (not_2_out, B);
  not not_3 (not_3_out, A);
  not not_4 (not_4_out, VEM_1);
  not not_5 (not_5_out, B);
  not not_6 (not_6_out, VEM_1);
  and and_1 (and_1_out, B, VEM_1);
  and and_2 (and_2_out, A, VEM_1);
  and and_3 (and_3_out, A, B);
  and and_4 (and_4_out, not_1_out, not_2_out, VEM_1);
  and and_5 (and_5_out, not_3_out, B, not_4_out);
  and and_6 (and_6_out, A, not_5_out, not_6_out);
  and and_7 (and_7_out, A, B, VEM_1);
  or or_1 (VAI_1, and_1_out, and_2_out, and_3_out);
  or or_2 (S, and_4_out, and_5_out, and_6_out, and_7_out);
endmodule

module main (
  input  [3:0] in_1,
  input  [3:0] in_2,
  output out_3,
  output [3:0] out_4
);

  ADD_4 add_4_1 (.OVERFLOW(out_3), .A(in_2), .out_4(out_4), .B(in_1));
  // Probe on out_4
endmodule

module ADD_2 (
  input  in_1
);
endmodule

module ADD_4 (
  input  [3:0] A,
  input  [3:0] B,
  output OVERFLOW,
  output [3:0] out_4
);

  wire add_1_2_vai_1, add_1_3_vai_1, add_1_4_vai_1;

  // Probe on B
  ADD_1 add_1_1 (.A(A[3]), .B(B[3]), .VEM_1(add_1_2_vai_1), .S(out_4[3]), .VAI_1(OVERFLOW));
  ADD_1 add_1_2 (.A(A[2]), .B(B[2]), .VEM_1(add_1_3_vai_1), .S(out_4[2]), .VAI_1(add_1_2_vai_1));
  ADD_1 add_1_3 (.A(A[1]), .B(B[1]), .VEM_1(add_1_4_vai_1), .S(out_4[1]), .VAI_1(add_1_3_vai_1));
  // Probe on out_4
  ADD_1 add_1_4 (.A(A[0]), .B(B[0]), .VEM_1(1'b0), .S(out_4[0]), .VAI_1(add_1_4_vai_1));
  // Probe on A
endmodule
