// Logisim project AULA LAB4 INCOMPLETO.circ as structural Verilog: 9 circuits, main circuit main
// Add-1
module ADD_1 (
  input  A,
  input  B,
  input  VEM_1,
  output S,
  output VAI_1
);

  wire and_1_out, and_2_out, and_3_out, and_4_out, and_5_out, and_6_out, and_7_out, not_1_out, not_2_out,
       not_3_out, not_4_out, not_5_out, not_6_out;

  not not_1 (not_1_out, A);
  not not_2 (not_2_out, B);
  not not_3 (not_3_out, A);
  not not_4 (not_4_out, VEM_1);
  not not_5 (not_5_out, B);
  not not_6 (not_6_out, VEM_1);
  and and_1 (and_1_out, B, VEM_1);
  and and_2 (and_2_out, A, VEM_1);
  and and_3 (and_3_out, A, B);
  and and_4 (and_4_out, not_1_out, not_2_out, VEM_1);
  and and_5 (and_5_out, not_3_out, B, not_4_out);
  and and_6 (and_6_out, A, not_5_out, not_6_out);
  and and_7 (and_7_out, A, B, VEM_1);
  or or_1 (VAI_1, and_1_out, and_2_out, and_3_out);
  or or_2 (S, and_4_out, and_5_out, and_6_out, and_7_out);
endmodule

module main (
  input  [3:0] B,
  input  [3:0] A,
  input  [3:0] in_3,
  input  [2:0] in_4,
  output out_5
);

  wire decodificador_1_a, decodificador_1_b, decodificador_1_c, decodificador_1_d;
  wire [3:0] add_4_1_out_4, b_4_out_3, or_1_out_3;

  DECODIFICADOR decodificador_1 (
    .in_1(in_4), .a(decodificador_1_a), .b(decodificador_1_b), .c(decodificador_1_c), .d(decodificador_1_d));  // open: e, f, g, h
  B b_1 (.in_1(in_3), .in_2(decodificador_1_a), .out_3(A));
  ADD_4 add_4_1 (.OVERFLOW(out_5), .A(A), .out_4(add_4_1_out_4), .B(B));
  B b_2 (.in_1(in_3), .in_2(decodificador_1_b), .out_3(add_4_1_out_4));
  OR or_1 (.A(B), .out_3(or_1_out_3), .B(A));
  B b_3 (.in_1(in_3), .in_2(decodificador_1_c), .out_3(or_1_out_3));
  NOT not_1 (.in_1(B), .in_2(b_4_out_3));
  B b_4 (.in_1(in_3), .in_2(decodificador_1_d), .out_3(b_4_out_3));
endmodule

module ADD_2 (
  input  in_1
);
endmodule

module ADD_4 (
  input  [3:0] A,
  input  [3:0] B,
  output OVERFLOW,
  output [3:0] out_4
);

  wire add_1_2_vai_1, add_1_3_vai_1, add_1_4_vai_1;

  // Probe on B
  ADD_1 add_1_1 (.A(A[3]), .B(B[3]), .VEM_1(add_1_2_vai_1), .S(out_4[3]), .VAI_1(OVERFLOW));
  ADD_1 add_1_2 (.A(A[2]), .B(B[2]), .VEM_1(add_1_3_vai_1), .S(out_4[2]), .VAI_1(add_1_2_vai_1));
  ADD_1 add_1_3 (.A(A[1]), .B(B[1]), .VEM_1(add_1_4_vai_1), .S(out_4[1]), .VAI_1(add_1_3_vai_1));
  // Probe on out_4
  ADD_1 add_1_4 (.A(A[0]), .B(B[0]), .VEM_1(1'b0), .S(out_4[0]), .VAI_1(add_1_4_vai_1));
  // Probe on A
endmodule

module DECODIFICADOR (
  input  [2:0] in_1,
  output a,
  output b,
  output c,
  output d,
  output e,
  output f,
  output g,
  output h
);

  wire not_1_out, not_2_out, not_3_out, not_4_out, not_5_out, not_6_out, not_7_out, not_8_out, not_9_out,
       not_10_out, not_11_out, not_12_out;

  not not_1 (not_1_out, in_1[2]);
  not not_2 (not_2_out, in_1[1]);
  not not_3 (not_3_out, in_1[0]);
  not not_4 (not_4_out, in_1[2]);
  not not_5 (not_5_out, in_1[1]);
  not not_6 (not_6_out, in_1[2]);
  not not_7 (not_7_out, in_1[0]);
  not not_8 (not_8_out, in_1[2]);
  not not_9 (not_9_out, in_1[1]);
  not not_10 (not_10_out, in_1[0]);
  not not_11 (not_11_out, in_1[1]);
  not not_12 (not_12_out, in_1[0]);
  and and_1 (h, in_1[2], in_1[1], in_1[0]);
  and and_2 (a, not_1_out, not_2_out, not_3_out);
  and and_3 (b, not_4_out, not_5_out, in_1[0]);
  and and_4 (c, not_6_out, in_1[1], not_7_out);
  and and_5 (d, not_8_out, in_1[1], in_1[0]);
  and and_6 (e, in_1[2], not_9_out, not_10_out);
  and and_7 (f, in_1[2], not_11_out, in_1[0]);
  and and_8 (g, in_1[2], in_1[1], not_12_out);
endmodule

module OR (
  input  [3:0] A,
  input  [3:0] B,
  output [3:0] out_3
);

  or or_1 (out_3[2], A[2], B[2]);
  or or_2 (out_3[3], A[3], B[3]);
  or or_3 (out_3[1], A[1], B[1]);
  or or_4 (out_3[0], A[0], B[0]);
endmodule

module NOT (
  input  [3:0] in_1,
  input  [3:0] in_2
);

  wire [3:0] not_3_out;

  not not_1 (not_3_out[3], in_1[3]);
  not not_2 (not_3_out[2], in_1[2]);
  // Probe on not_3_out
  not not_3 (not_3_out[0], in_1[0]);
  not not_4 (not_3_out[1], in_1[1]);
endmodule

module B (
  input  [3:0] in_1,
  input  in_2,
  output [3:0] out_3
);

  wire [3:0] controlled_buffer_4_out;

  assign controlled_buffer_4_out[3] = in_2 ? in_1[3] : 1'bz;  // Controlled_Buffer controlled_buffer_1
  assign controlled_buffer_4_out[2] = in_2 ? in_1[2] : 1'bz;  // Controlled_Buffer controlled_buffer_2
  // Probe on controlled_buffer_4_out
  assign controlled_buffer_4_out[1] = in_2 ? in_1[1] : 1'bz;  // Controlled_Buffer controlled_buffer_3
  assign controlled_buffer_4_out[0] = in_2 ? in_1[0] : 1'bz;  // Controlled_Buffer controlled_buffer_4
endmodule

module ROT (
  input  [1:0] in_1,
  input  [3:0] in_2,
  output [3:0] ABCD
);

  wire and_1_out, and_2_out, and_3_out, and_4_out, and_5_out, and_6_out, and_7_out, and_8_out, and_9_out;

  and and_1 (and_1_out, ~in_1[1], ~in_1[0], in_2[3]);  // AND_Gate
  and and_2 (and_2_out, ~in_1[1], in_1[0], in_2[2]);  // AND_Gate
  and and_3 (and_3_out, in_1[1], ~in_1[0], in_2[1]);  // AND_Gate
  and and_4 (and_4_out, in_1[1], in_1[0], in_2[0]);
  and and_5 (and_5_out, ~in_1[1], ~in_1[0], in_2[2]);  // AND_Gate
  and and_6 (and_6_out, ~in_1[1], in_1[0], in_2[1]);  // AND_Gate
  and and_7 (and_7_out, in_1[1], ~in_1[0], in_2[0]);  // AND_Gate
  and and_8 (and_8_out, ~in_1[1], ~in_1[0], in_2[1]);  // AND_Gate
  and and_9 (and_9_out, ~in_1[1], in_1[0], in_2[0]);  // AND_Gate
  and and_10 (ABCD[0], ~in_1[1], ~in_1[0], in_2[0]);  // AND_Gate
  or or_1 (ABCD[2], and_5_out, and_6_out, and_7_out);
  or or_2 (ABCD[1], and_8_out, and_9_out);
  or or_3 (ABCD[3], and_1_out, and_2_out, and_3_out, and_4_out);
endmodule
