// Logisim project AULA LAB9.circ as structural Verilog: 17 circuits, main circuit ULA
module Main (
  input  in_1,
  input  in_2,
  input  [3:0] in_3
);

  wire clock_1_out, not_1_out, not_2_out, RESET_out, uc_1_ac, uc_1_e, uc_1_ir, uc_1_pc, uc_1_ram,
       ula_1_overflow, ula_1_zero;
  wire [2:0] uc_1_opcode;
  wire [3:0] ac_1_out_3, counter_1_q, mux_1_out_4, ram_2_data, uc_1_operando, ula_1_out_6;
  wire [7:0] ir_1_q, ram_1_data;

  not not_1 (not_1_out, in_2);
  RAM #(.addrWidth(4)) ram_1 (.addr(counter_1_q), .data(ram_1_data));  // open: sel, clk, ld, clr
  Counter #(.width(4), .max('hf)) counter_1 (
    .D(in_3), .count(not_1_out), .Q(counter_1_q), .clk(uc_1_pc));  // open: load, carry, clr
  UC uc_1 (
    .OPERANDO(uc_1_operando), .E(uc_1_e), .OPCODE(uc_1_opcode), .\INSTRUÇÃO (ir_1_q), .IR(uc_1_ir),
    .PC(uc_1_pc), .AC(uc_1_ac), .RAM(uc_1_ram), .Clock(clock_1_out), .in_3(RESET_out));  // open: out_6
  Button RESET (.out(RESET_out));
  Clock clock_1 (.out(clock_1_out));
  IR ir_1 (.Clock(uc_1_ir), .Q(ir_1_q), .E(ram_1_data));
  // Probe on ac_1_out_3
  ULA ula_1 (
    .D(uc_1_e), .B(mux_1_out_4), .A(ac_1_out_3), .in_4(uc_1_opcode), .ZERO(ula_1_zero),
    .OVERFLOW(ula_1_overflow), .out_6(ula_1_out_6));
  AC ac_1 (.in_1(uc_1_ac), .out_3(ac_1_out_3), .in_2(ula_1_out_6));
  RAM #(.addrWidth(4), .dataWidth(4)) ram_2 (
    .addr(uc_1_operando), .data(ram_2_data), .sel(uc_1_ram), .clk(uc_1_ram), .ld(in_1));  // open: clr
  MUX mux_1 (.in_3(uc_1_e), .in_1(uc_1_operando), .in_2(ram_2_data), .out_4(mux_1_out_4));
  B b_1 (.E(ac_1_out_3), .C(not_2_out), .S(ram_2_data));
  D_Flip_Flop d_ff_1 (.clk(uc_1_ac), .D(ula_1_overflow));  // open: Q, Qn, preset, en, reset
  D_Flip_Flop d_ff_2 (.clk(uc_1_ac), .D(ula_1_zero));  // open: Q, Qn, preset, en, reset
  not not_2 (not_2_out, in_1);
endmodule

// Add-1
module ADD_1 (
  input  A,
  input  B,
  input  VEM_1,
  output S,
  output VAI_1
);

  wire and_1_out, and_2_out, and_3_out, and_4_out, and_5_out, and_6_out, and_7_out, not_1_out, not_2_out,
       not_3_out, not_4_out, not_5_out, not_6_out;

  not not_1 (not_1_out, A);
  not not_2 (not_2_out, B);
  not not_3 (not_3_out, A);
  not not_4 (not_4_out, VEM_1);
  not not_5 (not_5_out, B);
  not not_6 (not_6_out, VEM_1);
  and and_1 (and_1_out, B, VEM_1);
  and and_2 (and_2_out, A, VEM_1);
  and and_3 (and_3_out, A, B);
  and and_4 (and_4_out, not_1_out, not_2_out, VEM_1);
  and and_5 (and_5_out, not_3_out, B, not_4_out);
  and and_6 (and_6_out, A, not_5_out, not_6_out);
  and and_7 (and_7_out, A, B, VEM_1);
  or or_1 (VAI_1, and_1_out, and_2_out, and_3_out);
  or or_2 (S, and_4_out, and_5_out, and_6_out, and_7_out);
endmodule

module ULA (
  input  D,
  input  [3:0] B,
  input  [3:0] A,
  input  [2:0] in_4,
  output OVERFLOW,
  output [3:0] out_6,
  output ZERO
);

  wire add_4_1_overflow, and_1_out, and_2_out, decodificador_1_a, decodificador_1_b, decodificador_1_c,
       decodificador_1_d, decodificador_1_e, decodificador_1_f, decodificador_1_g, decodificador_1_h,
       not_2_out, sub_4_1_overflow;
  wire [3:0] add_4_1_out_4, b_6_s, not_1_s, or_2_out_3, rotd_1_abcd, rote_1_abcd, sub_4_1_out_4;

  or or_1 (OVERFLOW, and_1_out, and_2_out);
  and and_1 (and_1_out, add_4_1_overflow, decodificador_1_b);
  and and_2 (and_2_out, sub_4_1_overflow, decodificador_1_c);
  DECODIFICADOR decodificador_1 (
    .in_1(in_4), .a(decodificador_1_a), .b(decodificador_1_b), .c(decodificador_1_c), .d(decodificador_1_d),
    .e(decodificador_1_e), .f(decodificador_1_f), .g(decodificador_1_g), .h(decodificador_1_h));
  B b_1 (.E(B), .C(decodificador_1_a), .S(out_6));
  ADD_4 add_4_1 (.OVERFLOW(add_4_1_overflow), .A(A), .out_4(add_4_1_out_4), .B(B));
  SUB_4 sub_4_1 (.OVERFLOW(sub_4_1_overflow), .A(A), .out_4(sub_4_1_out_4), .B(B));
  B b_2 (.E(add_4_1_out_4), .C(decodificador_1_b), .S(out_6));
  OR or_2 (.A(B), .out_3(or_2_out_3), .B(A));
  B b_3 (.E(or_2_out_3), .C(decodificador_1_d), .S(out_6));
  B b_4 (.E(sub_4_1_out_4), .C(decodificador_1_c), .S(out_6));
  and and_3 (ZERO, ~out_6[0], ~out_6[1], ~out_6[2], ~out_6[3], ~decodificador_1_g, ~decodificador_1_h);  // AND_Gate
  NOT not_1 (.E(B), .S(not_1_s));
  B b_5 (.E(not_1_s), .C(decodificador_1_e), .S(out_6));
  ROTE rote_1 (.in_2(A), .in_1(B[1:0]), .ABCD(rote_1_abcd));
  ROTD rotd_1 (.in_2(A), .in_1(B[1:0]), .ABCD(rotd_1_abcd));
  B b_6 (.E(rote_1_abcd), .C(not_2_out), .S(b_6_s));
  not not_2 (not_2_out, D);
  B b_7 (.E(rotd_1_abcd), .C(D), .S(b_6_s));
  B b_8 (.E(b_6_s), .C(decodificador_1_f), .S(out_6));
endmodule

module ADD_2 (
  input  in_1
);
endmodule

module ADD_4 (
  input  [3:0] A,
  input  [3:0] B,
  output OVERFLOW,
  output [3:0] out_4
);

  wire add_1_2_vai_1, add_1_3_vai_1, add_1_4_vai_1;

  // Probe on B
  ADD_1 add_1_1 (.A(A[3]), .B(B[3]), .VEM_1(add_1_2_vai_1), .S(out_4[3]), .VAI_1(OVERFLOW));
  ADD_1 add_1_2 (.A(A[2]), .B(B[2]), .VEM_1(add_1_3_vai_1), .S(out_4[2]), .VAI_1(add_1_2_vai_1));
  ADD_1 add_1_3 (.A(A[1]), .B(B[1]), .VEM_1(add_1_4_vai_1), .S(out_4[1]), .VAI_1(add_1_3_vai_1));
  // Probe on out_4
  ADD_1 add_1_4 (.A(A[0]), .B(B[0]), .VEM_1(1'b0), .S(out_4[0]), .VAI_1(add_1_4_vai_1));
  // Probe on A
endmodule

module DECODIFICADOR (
  input  [2:0] in_1,
  output a,
  output b,
  output c,
  output d,
  output e,
  output f,
  output g,
  output h
);

  wire not_1_out, not_2_out, not_3_out, not_4_out, not_5_out, not_6_out, not_7_out, not_8_out, not_9_out,
       not_10_out, not_11_out, not_12_out;

  not not_1 (not_1_out, in_1[2]);
  not not_2 (not_2_out, in_1[1]);
  not not_3 (not_3_out, in_1[0]);
  not not_4 (not_4_out, in_1[2]);
  not not_5 (not_5_out, in_1[1]);
  not not_6 (not_6_out, in_1[2]);
  not not_7 (not_7_out, in_1[0]);
  not not_8 (not_8_out, in_1[2]);
  not not_9 (not_9_out, in_1[1]);
  not not_10 (not_10_out, in_1[0]);
  not not_11 (not_11_out, in_1[1]);
  not not_12 (not_12_out, in_1[0]);
  and and_1 (h, in_1[2], in_1[1], in_1[0]);
  and and_2 (a, not_1_out, not_2_out, not_3_out);
  and and_3 (b, not_4_out, not_5_out, in_1[0]);
  and and_4 (c, not_6_out, in_1[1], not_7_out);
  and and_5 (d, not_8_out, in_1[1], in_1[0]);
  and and_6 (e, in_1[2], not_9_out, not_10_out);
  and and_7 (f, in_1[2], not_11_out, in_1[0]);
  and and_8 (g, in_1[2], in_1[1], not_12_out);
endmodule

module OR (
  input  [3:0] A,
  input  [3:0] B,
  output [3:0] out_3
);

  or or_1 (out_3[2], A[2], B[2]);
  or or_2 (out_3[3], A[3], B[3]);
  or or_3 (out_3[1], A[1], B[1]);
  or or_4 (out_3[0], A[0], B[0]);
endmodule

module NOT (
  input  [3:0] E,
  output [3:0] S
);

  not not_1 (S[3], E[3]);
  not not_2 (S[2], E[2]);
  // Probe on S
  not not_3 (S[1], E[1]);
  not not_4 (S[0], E[0]);
endmodule

module B (
  input  [3:0] E,
  input  C,
  output [3:0] S
);

  assign S[3] = C ? E[3] : 1'bz;  // Controlled_Buffer controlled_buffer_1
  assign S[2] = C ? E[2] : 1'bz;  // Controlled_Buffer controlled_buffer_2
  // Probe on S
  assign S[1] = C ? E[1] : 1'bz;  // Controlled_Buffer controlled_buffer_3
  assign S[0] = C ? E[0] : 1'bz;  // Controlled_Buffer controlled_buffer_4
endmodule

module ROTD (
  input  [1:0] in_1,
  input  [3:0] in_2,
  output [3:0] ABCD
);

  wire and_1_out, and_2_out, and_3_out, and_4_out, and_5_out, and_6_out, and_7_out, and_8_out, and_9_out;

  and and_1 (and_1_out, ~in_1[1], ~in_1[0], in_2[0]);  // AND_Gate
  and and_2 (and_2_out, ~in_1[1], in_1[0], in_2[1]);  // AND_Gate
  and and_3 (and_3_out, in_1[1], ~in_1[0], in_2[2]);  // AND_Gate
  and and_4 (and_4_out, in_1[1], in_1[0], in_2[3]);
  and and_5 (and_5_out, ~in_1[1], ~in_1[0], in_2[1]);  // AND_Gate
  and and_6 (and_6_out, ~in_1[1], in_1[0], in_2[2]);  // AND_Gate
  and and_7 (and_7_out, in_1[1], ~in_1[0], in_2[3]);  // AND_Gate
  and and_8 (and_8_out, ~in_1[1], ~in_1[0], in_2[2]);  // AND_Gate
  and and_9 (and_9_out, ~in_1[1], in_1[0], in_2[3]);  // AND_Gate
  and and_10 (ABCD[3], ~in_1[1], ~in_1[0], in_2[3]);  // AND_Gate
  or or_1 (ABCD[1], and_5_out, and_6_out, and_7_out);
  or or_2 (ABCD[2], and_8_out, and_9_out);
  or or_3 (ABCD[0], and_1_out, and_2_out, and_3_out, and_4_out);
endmodule

module ROTE (
  input  [1:0] in_1,
  input  [3:0] in_2,
  output [3:0] ABCD
);

  wire and_1_out, and_2_out, and_3_out, and_4_out, and_5_out, and_6_out, and_7_out, and_8_out, and_9_out;

  and and_1 (and_1_out, ~in_1[1], ~in_1[0], in_2[3]);  // AND_Gate
  and and_2 (and_2_out, ~in_1[1], in_1[0], in_2[2]);  // AND_Gate
  and and_3 (and_3_out, in_1[1], ~in_1[0], in_2[1]);  // AND_Gate
  and and_4 (and_4_out, in_1[1], in_1[0], in_2[0]);
  and and_5 (and_5_out, ~in_1[1], ~in_1[0], in_2[2]);  // AND_Gate
  and and_6 (and_6_out, ~in_1[1], in_1[0], in_2[1]);  // AND_Gate
  and and_7 (and_7_out, in_1[1], ~in_1[0], in_2[0]);  // AND_Gate
  and and_8 (and_8_out, ~in_1[1], ~in_1[0], in_2[1]);  // AND_Gate
  and and_9 (and_9_out, ~in_1[1], in_1[0], in_2[0]);  // AND_Gate
  and and_10 (ABCD[0], ~in_1[1], ~in_1[0], in_2[0]);  // AND_Gate
  or or_1 (ABCD[2], and_5_out, and_6_out, and_7_out);
  or or_2 (ABCD[1], and_8_out, and_9_out);
  or or_3 (ABCD[3], and_1_out, and_2_out, and_3_out, and_4_out);
endmodule

module SUB_1 (
  input  A,
  input  B,
  input  VEM_1,
  output SUB,
  output VAI_1
);

  wire and_1_out, and_2_out, and_3_out, and_4_out, and_5_out, and_6_out, and_7_out, not_1_out, not_2_out,
       not_3_out, not_4_out, not_5_out, not_6_out, not_7_out, not_8_out;

  not not_1 (not_1_out, A);
  not not_2 (not_2_out, B);
  not not_3 (not_3_out, A);
  not not_4 (not_4_out, VEM_1);
  not not_5 (not_5_out, B);
  not not_6 (not_6_out, VEM_1);
  not not_7 (not_7_out, A);
  not not_8 (not_8_out, A);
  and and_1 (and_1_out, not_1_out, not_2_out, VEM_1);
  and and_2 (and_2_out, not_3_out, B, not_4_out);
  and and_3 (and_3_out, A, not_5_out, not_6_out);
  and and_4 (and_4_out, A, B, VEM_1);
  and and_5 (and_5_out, not_7_out, VEM_1);
  and and_6 (and_6_out, not_8_out, B);
  and and_7 (and_7_out, B, VEM_1);
  or or_1 (SUB, and_1_out, and_2_out, and_3_out, and_4_out);
  or or_2 (VAI_1, and_5_out, and_6_out, and_7_out);
endmodule

module SUB_4 (
  input  [3:0] A,
  input  [3:0] B,
  output OVERFLOW,
  output [3:0] out_4
);

  wire sub_1_2_vai_1, sub_1_3_vai_1, sub_1_4_vai_1;

  // Probe on B
  SUB_1 sub_1_1 (.A(A[3]), .B(B[3]), .VEM_1(sub_1_2_vai_1), .SUB(out_4[3]), .VAI_1(OVERFLOW));
  SUB_1 sub_1_2 (.A(A[2]), .B(B[2]), .VEM_1(sub_1_3_vai_1), .SUB(out_4[2]), .VAI_1(sub_1_2_vai_1));
  SUB_1 sub_1_3 (.A(A[1]), .B(B[1]), .VEM_1(sub_1_4_vai_1), .SUB(out_4[1]), .VAI_1(sub_1_3_vai_1));
  // Probe on out_4
  SUB_1 sub_1_4 (.A(A[0]), .B(B[0]), .VEM_1(1'b0), .SUB(out_4[0]), .VAI_1(sub_1_4_vai_1));
  // Probe on A
endmodule

module MUX (
  input  [3:0] in_1,
  input  [3:0] in_2,
  input  in_3,
  output [3:0] out_4
);

  wire not_1_out;

  not not_1 (not_1_out, in_3);
  B b_1 (.E(in_1), .C(not_1_out), .S(out_4));
  B b_2 (.E(in_2), .C(in_3), .S(out_4));
endmodule

module AC (
  input  in_1,
  input  [3:0] in_2,
  output [3:0] out_3
);

  D_Flip_Flop d_ff_1 (.clk(in_1), .D(in_2[3]), .Q(out_3[3]));  // open: Qn, preset, en, reset
  D_Flip_Flop d_ff_2 (.clk(in_1), .D(in_2[2]), .Q(out_3[2]));  // open: Qn, preset, en, reset
  D_Flip_Flop d_ff_3 (.clk(in_1), .D(in_2[1]), .Q(out_3[1]));  // open: Qn, preset, en, reset
  D_Flip_Flop d_ff_4 (.clk(in_1), .D(in_2[0]), .Q(out_3[0]));  // open: Qn, preset, en, reset
endmodule

module IR (
  input  Clock,
  input  [7:0] E,
  output [7:0] Q
);

  D_Flip_Flop #(.trigger("falling")) d_ff_1 (.clk(Clock), .D(E[7]), .Q(Q[7]));  // open: Qn, preset, en, reset
  D_Flip_Flop #(.trigger("falling")) d_ff_2 (.clk(Clock), .D(E[6]), .Q(Q[6]));  // open: Qn, preset, en, reset
  D_Flip_Flop #(.trigger("falling")) d_ff_3 (.clk(Clock), .D(E[5]), .Q(Q[5]));  // open: Qn, preset, en, reset
  D_Flip_Flop #(.trigger("falling")) d_ff_4 (.clk(Clock), .D(E[4]), .Q(Q[4]));  // open: Qn, preset, en, reset
  D_Flip_Flop #(.trigger("falling")) d_ff_5 (.clk(Clock), .D(E[3]), .Q(Q[3]));  // open: Qn, preset, en, reset
  D_Flip_Flop #(.trigger("falling")) d_ff_6 (.clk(Clock), .D(E[2]), .Q(Q[2]));  // open: Qn, preset, en, reset
  D_Flip_Flop #(.trigger("falling")) d_ff_7 (.clk(Clock), .D(E[0]), .Q(Q[0]));  // open: Qn, preset, en, reset
  D_Flip_Flop #(.trigger("falling")) d_ff_8 (.clk(Clock), .D(E[1]), .Q(Q[1]));  // open: Qn, preset, en, reset
endmodule

module UC (
  input  [7:0] \INSTRUÇÃO ,
  input  Clock,
  input  in_3,
  output [3:0] OPERANDO,
  output E,
  output out_6,
  output [2:0] OPCODE,
  output IR,
  output PC,
  output AC,
  output RAM
);

  wire [1:0] counter_1_q;

  Counter #(.width(2), .max('h3)) counter_1 (.Q(counter_1_q), .clk(Clock), .clr(in_3));  // open: load, D, count, carry
  and and_1 (IR, ~counter_1_q[1], ~counter_1_q[0]);  // AND_Gate
  and and_2 (PC, ~counter_1_q[1], counter_1_q[0]);  // AND_Gate
  and and_3 (AC, counter_1_q[1], ~counter_1_q[0]);  // AND_Gate
  and and_4 (RAM, counter_1_q[1], counter_1_q[0]);

  assign E = \INSTRUÇÃO [4];
  assign OPCODE = \INSTRUÇÃO [7:5];
  assign OPERANDO = \INSTRUÇÃO [3:0];
  assign out_6 = in_3;
endmodule
